// Digital circuit COMPUTER.dig as structural Verilog
module COMPUTER (
  input  CLK,
  input  [15:0] INSTR,
  output [7:0] out_3,
  output [7:0] out_4,
  output [7:0] out_5
);

  wire alu_8_1_p5, alu_8_1_p6, cmpu_ctrl_1_p4, ctrl_unit_1_p2, ctrl_unit_1_p3, ctrl_unit_1_p4,
       ctrl_unit_1_p5, ctrl_unit_1_p6, ctrl_unit_1_p7, ctrl_unit_1_p8, ctrl_unit_1_p11;
  wire [1:0] ctrl_unit_1_p10, ctrl_unit_1_p12;
  wire [7:0] _8_register_bank_1_p4, _256b_mem_1_rd, alu_8_1_p4, ctrl_unit_1_p9, multiplexer_1_out,
       multiplexer_2_out, multiplexer_4_out, PC_plus_1_s, PC_plus_Imm_s;

  Multiplexer #(.Selector_Bits(2), .Bits(8)) multiplexer_1 (
    .sel(ctrl_unit_1_p12), .in_0(PC_plus_1_s), .in_1(ctrl_unit_1_p9), .in_2(out_3), .in_3(multiplexer_4_out),
    .out(multiplexer_1_out));
  REGISTER_8 PC (.D(multiplexer_1_out), .E(1'b1), .CLK(CLK), .Q(out_5));
  // CTRL_UNIT ctrl_unit_1: pin names not known; wires that end beside it: INSTR, ctrl_unit_1_p2, ctrl_unit_1_p3, ctrl_unit_1_p4, ctrl_unit_1_p5, ctrl_unit_1_p6, ctrl_unit_1_p7, ctrl_unit_1_p8, ctrl_unit_1_p9, ctrl_unit_1_p10, ctrl_unit_1_p11, ctrl_unit_1_p12
  ADD_8 PC_plus_1 (.Cin(1'b0), .A(out_5), .B(8'h1), .S(PC_plus_1_s));  // open: Cout
  ADD_8 PC_plus_Imm (.Cin(1'b0), .A(ctrl_unit_1_p9), .B(out_5), .S(PC_plus_Imm_s));  // open: Cout
  // _8_REGISTER_BANK _8_register_bank_1: pin names not known; wires that end beside it: ctrl_unit_1_p3, ctrl_unit_1_p4, ctrl_unit_1_p5, _8_register_bank_1_p4, ctrl_unit_1_p6, CLK, out_3, out_4
  Multiplexer #(.Bits(8)) multiplexer_2 (
    .sel(ctrl_unit_1_p8), .in_0(out_4), .in_1(ctrl_unit_1_p9), .out(multiplexer_2_out));
  // ALU_8 alu_8_1: pin names not known; wires that end beside it: out_3, multiplexer_2_out, ctrl_unit_1_p7, alu_8_1_p4, alu_8_1_p5, alu_8_1_p6
  // CMPU_CTRL cmpu_ctrl_1: pin names not known; wires that end beside it: ctrl_unit_1_p2, alu_8_1_p5, alu_8_1_p6, cmpu_ctrl_1_p4
  _256B_MEM _256b_mem_1 (.A(alu_8_1_p4), .WD(out_4), .WE(ctrl_unit_1_p11), .CLK(CLK), .RD(_256b_mem_1_rd));
  Multiplexer #(.Selector_Bits(2), .Bits(8)) multiplexer_3 (
    .sel(ctrl_unit_1_p10), .in_0(alu_8_1_p4), .in_1(_256b_mem_1_rd), .in_2(PC_plus_1_s),
    .in_3(ctrl_unit_1_p9), .out(_8_register_bank_1_p4));
  Multiplexer #(.Bits(8)) multiplexer_4 (
    .sel(cmpu_ctrl_1_p4), .in_0(PC_plus_1_s), .in_1(PC_plus_Imm_s), .out(multiplexer_4_out));
endmodule
